// Logisim project adder3.circ as structural Verilog: 1 circuit, main circuit main
module main (
  input  B1,
  input  B2,
  input  B3,
  output SUCCESS,
  output SUCCESS_2
);

  wire and_1_out, and_2_out, xor_1_out;

  xor xor_1 (xor_1_out, B1, B2);
  and and_1 (and_1_out, B1, B2);
  xor xor_2 (SUCCESS, xor_1_out, B3);
  and and_2 (and_2_out, xor_1_out, B3);
  or or_1 (SUCCESS_2, and_2_out, and_1_out);

  // Notes on the sheet:
  //   vamos adicionar agora uma terceira entrada
endmodule
