// Logisim project contadorcresc.circ as structural Verilog: 1 circuit, main circuit main
module main (
  output Q2,
  output Q3,
  output Q0,
  output Q1
);

  wire and_1_out, and_2_out, CLK_out;

  Clock CLK (.out(CLK_out));
  J_K_Flip_Flop p (.J(1'b1), .clk(CLK_out), .K(1'b1), .Q(Q0));  // open: Qn, preset, en, reset
  J_K_Flip_Flop j_k_ff_1 (.J(Q0), .clk(CLK_out), .K(Q0), .Q(Q1));  // open: Qn, preset, en, reset
  and and_1 (and_1_out, Q0, Q1);
  J_K_Flip_Flop j_k_ff_2 (.J(and_1_out), .clk(CLK_out), .K(and_1_out), .Q(Q2));  // open: Qn, preset, en, reset
  and and_2 (and_2_out, and_1_out, Q2);
  J_K_Flip_Flop j_k_ff_3 (.J(and_2_out), .clk(CLK_out), .K(and_2_out), .Q(Q3));  // open: Qn, preset, en, reset
endmodule
