// Logisim project contadordesc.circ as structural Verilog: 1 circuit, main circuit main
module main (
  input  clk,
  output Q0,
  output Q1,
  output Q2
);

  wire and_1_out, j_k_ff_3_qn;

  J_K_Flip_Flop j_k_ff_1 (.J(1'b1), .clk(clk), .K(1'b1), .Qn(Q0));  // open: Q, preset, en, reset
  and and_1 (and_1_out, Q0, Q1);
  J_K_Flip_Flop j_k_ff_2 (.J(Q0), .clk(clk), .K(Q0), .Qn(Q1));  // open: Q, preset, en, reset
  J_K_Flip_Flop j_k_ff_3 (.J(and_1_out), .clk(clk), .K(and_1_out), .Qn(j_k_ff_3_qn));  // open: Q, preset, en, reset
  and and_2 (Q2, and_1_out, j_k_ff_3_qn);
  J_K_Flip_Flop j_k_ff_4 (.J(Q2), .clk(clk), .K(Q2));  // open: Q, Qn, preset, en, reset
endmodule
