// Logisim project crescent-count.circ as structural Verilog: 1 circuit, main circuit main
module main (
  input  Clock,
  output _4,
  output _8,
  output _1,
  output _2
);

  wire and_1_out, and_2_out;

  J_K_Flip_Flop p (.J(1'b1), .clk(Clock), .K(1'b1), .Q(_1));  // open: Qn, preset, en, reset
  J_K_Flip_Flop j_k_ff_1 (.J(_1), .clk(Clock), .K(_1), .Q(_2));  // open: Qn, preset, en, reset
  and and_1 (and_1_out, _1, _2);
  J_K_Flip_Flop j_k_ff_2 (.J(and_1_out), .clk(Clock), .K(and_1_out), .Q(_4));  // open: Qn, preset, en, reset
  and and_2 (and_2_out, and_1_out, _4);
  J_K_Flip_Flop j_k_ff_3 (.J(and_2_out), .clk(Clock), .K(and_2_out), .Q(_8));  // open: Qn, preset, en, reset
  // AND_Gate and_3 is placed but not wired
endmodule
