// Logisim project contadorcresc.circ as structural Verilog: 1 circuit, main circuit main
module main (
  input  CLK,
  input  RST,
  output Q0,
  output Q1,
  output Q2,
  output Q3
);

  wire and_1_out, and_2_out, and_3_out, or_1_out;

  J_K_Flip_Flop j_k_ff_1 (.J(1'b1), .clk(CLK), .K(1'b1), .Q(Q0), .reset(or_1_out));  // open: Qn, preset, en
  or or_1 (or_1_out, RST, and_1_out);
  and and_1 (and_1_out, Q1, Q3);
  J_K_Flip_Flop j_k_ff_2 (.J(Q0), .clk(CLK), .K(Q0), .Q(Q1), .reset(or_1_out));  // open: Qn, preset, en
  and and_2 (and_2_out, Q0, Q1);
  J_K_Flip_Flop j_k_ff_3 (.J(and_2_out), .clk(CLK), .K(and_2_out), .Q(Q2), .reset(or_1_out));  // open: Qn, preset, en
  and and_3 (and_3_out, and_2_out, Q2);
  J_K_Flip_Flop j_k_ff_4 (.J(and_3_out), .clk(CLK), .K(and_3_out), .Q(Q3), .reset(or_1_out));  // open: Qn, preset, en
endmodule
