// Logisim project edice.circ as structural Verilog: 1 circuit, main circuit main
module main (
  input  RST
);

  wire and_1_out, and_2_out, decodiicador7seg_1_a_2, decodiicador7seg_1_b_2, decodiicador7seg_1_c_2,
       decodiicador7seg_1_d_2, decodiicador7seg_1_e, decodiicador7seg_1_f, decodiicador7seg_1_g,
       decodiicador7seg_2_a_2, decodiicador7seg_2_b_2, decodiicador7seg_2_c_2, decodiicador7seg_2_d_2,
       decodiicador7seg_2_e, decodiicador7seg_2_f, decodiicador7seg_2_g, main_1_q0, main_1_q1, main_1_q2,
       main_1_q3, main_2_q0, main_2_q1, main_2_q2, main_2_q3, not_1_out, not_2_out, or_1_out, or_2_out,
       SD1_out, SD2_out;

  Clock SD1 (.out(SD1_out));
  Clock #(.lowDuration(3)) SD2 (.out(SD2_out));
  and and_1 (and_1_out, not_2_out, main_2_q2, main_2_q1, main_2_q0);
  or or_1 (or_1_out, and_1_out, RST);
  and and_2 (and_2_out, not_1_out, main_1_q2, main_1_q1, main_1_q0);
  or or_2 (or_2_out, and_2_out, RST);
  not not_1 (not_1_out, main_1_q3);
  contadorcresc_main main_1 (
    .CLK(SD1_out), .RST(or_2_out), .Q0(main_1_q0), .Q1(main_1_q1), .Q2(main_1_q2), .Q3(main_1_q3));
  not not_2 (not_2_out, main_2_q3);
  contadorcresc_main main_2 (
    .CLK(SD2_out), .RST(or_1_out), .Q0(main_2_q0), .Q1(main_2_q1), .Q2(main_2_q2), .Q3(main_2_q3));
  DECODIICADOR7SEG decodiicador7seg_1 (
    .A(main_1_q3), .B(main_1_q2), .C(main_1_q1), .D(main_1_q0), .a_2(decodiicador7seg_1_a_2),
    .b_2(decodiicador7seg_1_b_2), .c_2(decodiicador7seg_1_c_2), .d_2(decodiicador7seg_1_d_2),
    .e(decodiicador7seg_1_e), .f(decodiicador7seg_1_f), .g(decodiicador7seg_1_g));
  DECODIICADOR7SEG decodiicador7seg_2 (
    .A(main_2_q3), .B(main_2_q2), .C(main_2_q1), .D(main_2_q0), .a_2(decodiicador7seg_2_a_2),
    .b_2(decodiicador7seg_2_b_2), .c_2(decodiicador7seg_2_c_2), .d_2(decodiicador7seg_2_d_2),
    .e(decodiicador7seg_2_e), .f(decodiicador7seg_2_f), .g(decodiicador7seg_2_g));
  _7_Segment_Display u_7_segment_display_1 (
    .g(decodiicador7seg_1_g), .f(decodiicador7seg_1_f), .a(decodiicador7seg_1_a_2),
    .b(decodiicador7seg_1_b_2), .e(decodiicador7seg_1_e), .d(decodiicador7seg_1_d_2),
    .c(decodiicador7seg_1_c_2));  // open: dp
  _7_Segment_Display u_7_segment_display_2 (
    .g(decodiicador7seg_2_g), .f(decodiicador7seg_2_f), .a(decodiicador7seg_2_a_2),
    .b(decodiicador7seg_2_b_2), .e(decodiicador7seg_2_e), .d(decodiicador7seg_2_d_2),
    .c(decodiicador7seg_2_c_2));  // open: dp

  // Notes on the sheet:
  //   aperte CTRL-K e depois de um tempo, CTRL-K de novo
  //   quando chegar no seis volte ao começo
  //   quando chegar no seis volte ao começo
  //   atividade corrigida pelo professor Cesar Giacomini Penteado, as 19:20 aprox dia 22/11/24
  //   atividade realizada por João Paulo Ferrari Sant'Ana as 10:47 do dia 20/11/2024
endmodule
