// Logisim project iseq.circ as structural Verilog: 1 circuit, main circuit main
module main (
  input  in_1,
  input  in_2,
  input  in_3,
  input  in_4,
  input  in_5,
  input  in_6,
  input  in_7,
  input  in_8,
  input  in_9,
  input  in_10,
  input  in_11,
  input  in_12,
  input  in_13,
  input  in_14,
  input  in_15,
  input  in_16,
  input  CLK,
  input  CLK_2,
  input  RST,
  input  RST_2
);

  wire main_1_q0, main_1_q1, main_1_q2, main_1_q3, main_1_q4, main_1_q5, main_1_q6, main_1_q7, main_2_out_17,
       main_3_q0, main_3_q1, main_3_q2, main_3_q3, main_3_q4, main_3_q5, main_3_q6, main_3_q7;

  numgen_main main_1 (
    .CLK(CLK), .RST(RST), .D0(in_9), .D1(in_10), .D2(in_11), .D3(in_12), .D4(in_13), .D5(in_14), .D6(in_15),
    .D7(in_16), .Q0(main_1_q0), .Q1(main_1_q1), .Q2(main_1_q2), .Q3(main_1_q3), .Q4(main_1_q4),
    .Q5(main_1_q5), .Q6(main_1_q6), .Q7(main_1_q7));
  eq_main main_2 (
    .A0(main_3_q0), .A1(main_3_q1), .A2(main_3_q2), .A3(main_3_q3), .A4(main_3_q4), .A5(main_3_q5),
    .A6(main_3_q6), .A7(main_3_q7), .B0(main_1_q0), .B1(main_1_q1), .B2(main_1_q2), .B3(main_1_q3),
    .B4(main_1_q4), .B5(main_1_q5), .B6(main_1_q6), .B7(main_1_q7), .out_17(main_2_out_17));
  LED led_1 (.in(main_2_out_17));
  numgen_main main_3 (
    .CLK(CLK_2), .RST(RST_2), .D0(in_1), .D1(in_2), .D2(in_3), .D3(in_4), .D4(in_5), .D5(in_6), .D6(in_7),
    .D7(in_8), .Q0(main_3_q0), .Q1(main_3_q1), .Q2(main_3_q2), .Q3(main_3_q3), .Q4(main_3_q4),
    .Q5(main_3_q5), .Q6(main_3_q6), .Q7(main_3_q7));
endmodule
