// Logisim project numgen.circ as structural Verilog: 1 circuit, main circuit main
module main (
  input  D0,
  input  D1,
  input  D2,
  input  D3,
  input  D4,
  input  D5,
  input  D6,
  input  D7,
  input  CLK,
  input  RST,
  output Q6,
  output Q7,
  output Q0,
  output Q1,
  output Q2,
  output Q3,
  output Q4,
  output Q5
);

  D_Flip_Flop d_ff_1 (.clk(CLK), .D(D0), .Q(Q0), .reset(RST));  // open: Qn, preset, en
  D_Flip_Flop d_ff_2 (.clk(CLK), .D(D1), .Q(Q1), .reset(RST));  // open: Qn, preset, en
  D_Flip_Flop d_ff_3 (.clk(CLK), .D(D2), .Q(Q2), .reset(RST));  // open: Qn, preset, en
  D_Flip_Flop d_ff_4 (.clk(CLK), .D(D3), .Q(Q3), .reset(RST));  // open: Qn, preset, en
  D_Flip_Flop d_ff_5 (.clk(CLK), .D(D4), .Q(Q4), .reset(RST));  // open: Qn, preset, en
  D_Flip_Flop d_ff_6 (.clk(CLK), .D(D5), .Q(Q5), .reset(RST));  // open: Qn, preset, en
  D_Flip_Flop d_ff_7 (.clk(CLK), .D(D6), .Q(Q6), .reset(RST));  // open: Qn, preset, en
  D_Flip_Flop d_ff_8 (.clk(CLK), .D(D7), .Q(Q7), .reset(RST));  // open: Qn, preset, en
endmodule
