// Logisim project paralel-entry-serial-exit.circ as structural Verilog: 1 circuit, main circuit main
module main (
  input  D0,
  input  D1,
  input  D2,
  input  D3,
  input  SHIFT_LOAD,
  input  CLK
);

  wire g1_out, g2_out, g3_out, g4_out, g5_out, g6_out, g7_out, not_1_out, or_1_out, or_2_out, or_3_out, Q0_q,
       Q1_2_q, Q1_q;

  D_Flip_Flop Q0 (.clk(CLK), .D(g1_out), .Q(Q0_q));  // open: Qn, preset, en, reset
  not not_1 (not_1_out, SHIFT_LOAD);
  and g1 (g1_out, D0, not_1_out);
  and g5 (g5_out, Q0_q, SHIFT_LOAD);
  and g2 (g2_out, not_1_out, D1);
  or or_1 (or_1_out, g5_out, g2_out);
  D_Flip_Flop Q1 (.clk(CLK), .D(or_1_out), .Q(Q1_q));  // open: Qn, preset, en, reset
  and g6 (g6_out, Q1_q, SHIFT_LOAD);
  and g3 (g3_out, not_1_out, D2);
  or or_2 (or_2_out, g6_out, g3_out);
  D_Flip_Flop Q1_2 (.clk(CLK), .D(or_2_out), .Q(Q1_2_q));  // open: Qn, preset, en, reset
  and g7 (g7_out, Q1_2_q, SHIFT_LOAD);
  and g4 (g4_out, not_1_out, D3);
  or or_3 (or_3_out, g7_out, g4_out);
  D_Flip_Flop Q1_3 (.clk(CLK), .D(or_3_out));  // open: Q, Qn, preset, en, reset
endmodule
