// Logisim project adder.circ as structural Verilog: 1 circuit, main circuit main
module main (
  input  B1,
  input  B2,
  output Q_SUCCESS
);

  xor xor_1 (Q_SUCCESS, B1, B2);

  // Notes on the sheet:
  //   a forma mais simples de adição (sem carry) é essa
endmodule
