// Logisim project adder2.circ as structural Verilog: 1 circuit, main circuit main
module main (
  input  B1,
  input  B2,
  output SUM,
  output CARRY
);

  xor xor_1 (SUM, B1, B2);
  and and_1 (CARRY, B1, B2);

  // Notes on the sheet:
  //   B1: pull=up
  //   o programa "adder" era só um adder sem carry
  //   agora iremos adicionar o carry
endmodule
