// Logisim project adder4.circ as structural Verilog: 1 circuit, main circuit main
module main (
  input  A,
  input  B,
  input  C,
  output out_4,
  output out_5,
  output out_6,
  output out_7,
  output S
);

  wire main_1_success_2, main_2_success_2, main_3_success_2;

  adder3_main main_1 (.B1(A), .B2(B), .B3(C), .SUCCESS(out_4), .SUCCESS_2(main_1_success_2));
  adder3_main main_2 (.B1(A), .B2(B), .B3(main_1_success_2), .SUCCESS(out_5), .SUCCESS_2(main_2_success_2));
  adder3_main main_3 (.B1(A), .B2(B), .B3(main_2_success_2), .SUCCESS(out_6), .SUCCESS_2(main_3_success_2));
  adder3_main main_4 (.B1(A), .B2(B), .B3(main_3_success_2), .SUCCESS(out_7), .SUCCESS_2(S));
endmodule
