// Logisim project eightbitaddr.circ as structural Verilog: 1 circuit, main circuit main
module main (
  input  A2,
  input  A3,
  input  A5,
  input  A6,
  input  A7,
  input  A0,
  input  A4,
  input  A1,
  input  B2,
  input  B3,
  input  B5,
  input  B6,
  input  B7,
  input  B0,
  input  B4,
  input  B1,
  input  C0,
  output S,
  output S_2,
  output S_3,
  output S_4,
  output S_5,
  output S_6,
  output S_7
);

  wire main_1_carry, main_2_carry, main_3_carry, main_4_carry, main_5_carry, main_6_carry, main_7_carry;

  fulladdr_main main_1 (.A(A0), .B(B0), .C(C0), .R(S), .CARRY(main_1_carry));
  fulladdr_main main_2 (.A(A1), .B(B1), .C(main_1_carry), .R(S_2), .CARRY(main_2_carry));
  fulladdr_main main_3 (.A(A2), .B(B2), .C(main_2_carry), .R(S_3), .CARRY(main_3_carry));
  fulladdr_main main_4 (.A(A3), .B(B3), .C(main_3_carry), .R(S_4), .CARRY(main_4_carry));
  fulladdr_main main_5 (.A(A4), .B(B4), .C(main_4_carry), .R(S_5), .CARRY(main_5_carry));
  fulladdr_main main_6 (.A(A5), .B(B5), .C(main_5_carry), .R(S_6), .CARRY(main_6_carry));
  fulladdr_main main_7 (.A(A6), .B(B6), .C(main_6_carry), .R(S_7), .CARRY(main_7_carry));
  fulladdr_main main_8 (.A(A7), .B(B7), .C(main_7_carry));  // open: R, CARRY

  // Notes on the sheet:
  //   B0
  //   B1
  //   B2
  //   B3
endmodule
