// Logisim project fullsubtr.circ as structural Verilog: 1 circuit, main circuit main
module main (
  input  C0,
  input  A3,
  input  A4,
  input  A5,
  input  A6,
  input  A7,
  input  A1,
  input  A2,
  input  B3,
  input  B4,
  input  B5,
  input  B6,
  input  B7,
  input  A0,
  input  B1,
  input  B2,
  input  B0,
  output D2,
  output D3,
  output D4,
  output D5,
  output D6,
  output D7,
  output D1,
  output D0
);

  wire main_1_c, main_1_d, main_2_c, main_3_c, main_3_d, main_4_c, main_5_c, main_5_d, main_6_c, main_7_c,
       main_7_d, main_8_c, main_9_c, main_9_d, main_10_c, main_11_c, main_11_d, main_12_c, main_13_c,
       main_13_d, main_14_c, main_15_c, main_15_d, main_16_c, or_1_out, or_2_out, or_3_out, or_4_out,
       or_5_out, or_6_out, or_7_out, or_8_out;

  subtr3_main main_1 (.A(A0), .B(B0), .D(main_1_d), .C(main_1_c));
  subtr3_main main_2 (.A(C0), .B(main_1_d), .D(D0), .C(main_2_c));
  or or_1 (or_1_out, main_2_c, main_1_c);
  subtr3_main main_3 (.A(A1), .B(B1), .D(main_3_d), .C(main_3_c));
  subtr3_main main_4 (.A(or_1_out), .B(main_3_d), .D(D1), .C(main_4_c));
  or or_2 (or_2_out, main_4_c, main_3_c);
  subtr3_main main_5 (.A(A2), .B(B2), .D(main_5_d), .C(main_5_c));
  subtr3_main main_6 (.A(or_2_out), .B(main_5_d), .D(D2), .C(main_6_c));
  or or_3 (or_3_out, main_6_c, main_5_c);
  subtr3_main main_7 (.A(A3), .B(B3), .D(main_7_d), .C(main_7_c));
  subtr3_main main_8 (.A(or_3_out), .B(main_7_d), .D(D3), .C(main_8_c));
  or or_4 (or_4_out, main_8_c, main_7_c);
  subtr3_main main_9 (.A(A4), .B(B4), .D(main_9_d), .C(main_9_c));
  subtr3_main main_10 (.A(or_4_out), .B(main_9_d), .D(D4), .C(main_10_c));
  or or_5 (or_5_out, main_10_c, main_9_c);
  subtr3_main main_11 (.A(A5), .B(B5), .D(main_11_d), .C(main_11_c));
  subtr3_main main_12 (.A(or_5_out), .B(main_11_d), .D(D5), .C(main_12_c));
  or or_6 (or_6_out, main_12_c, main_11_c);
  subtr3_main main_13 (.A(A6), .B(B6), .D(main_13_d), .C(main_13_c));
  subtr3_main main_14 (.A(or_6_out), .B(main_13_d), .D(D6), .C(main_14_c));
  or or_7 (or_7_out, main_14_c, main_13_c);
  subtr3_main main_15 (.A(A7), .B(B7), .D(main_15_d), .C(main_15_c));
  subtr3_main main_16 (.A(or_7_out), .B(main_15_d), .D(D7), .C(main_16_c));
  or or_8 (or_8_out, main_16_c, main_15_c);
  LED led_1 (.in(or_8_out));
endmodule
