// Logisim project subtr1.circ as structural Verilog: 1 circuit, main circuit main
module main (
  input  in_1,
  input  in_2,
  input  in_3,
  output out_4,
  output OK,
  output out_6,
  output out_7
);

  wire and_2_out, not_1_out, not_2_out;

  xor xor_1 (out_4, in_2, in_3);
  not not_1 (not_1_out, in_2);
  LED led_1 (.in(out_4));
  and and_1 (out_6, not_1_out, in_3);
  LED led_2 (.in(out_6));
  not not_2 (not_2_out, out_4);
  xor xor_2 (OK, in_1, out_4);
  and and_2 (and_2_out, not_2_out, in_1);
  LED led_3 (.in(OK));
  or or_1 (out_7, and_2_out, out_6);
  LED led_4 (.in(out_7));
endmodule
