// Logisim project parity.circ as structural Verilog: 1 circuit, main circuit main
module main (
  input  in_1,
  input  in_2,
  input  in_3,
  input  in_4,
  output out_5
);

  wire xor_1_out, xor_2_out;

  xor xor_1 (xor_1_out, in_1, in_2);
  xor xor_2 (xor_2_out, in_3, in_4);
  xor xor_3 (out_5, xor_1_out, xor_2_out);

  // Notes on the sheet:
  //   lógica obtida por ajuda do professor Cesar Giacomini Penteado dia 11/11/24 as aprox. 21:28
endmodule
