// Logisim project passwd.circ as structural Verilog: 1 circuit, main circuit main
module main (
  input  WRITE_PASS,
  input  CONFIG_PASS,
  input  CLEAR_PASS,
  input  RST_PASS,
  input  SET_PASS,
  input  SET_PASS_2
);

  wire CLK_out, clock_1_out, main_1_q0, main_1_q1, main_1_q2, main_1_q3, main_2_out_9, main_3_q0, main_3_q1,
       main_3_q2, main_3_q3;

  Clock clock_1 (.out(clock_1_out));
  word_main main_1 (
    .CLK(clock_1_out), .data_in(CONFIG_PASS), .RST(RST_PASS), .HLD(SET_PASS_2), .Q0(main_1_q0),
    .Q1(main_1_q1), .Q2(main_1_q2), .Q3(main_1_q3));
  equals_main main_2 (
    .A0(main_3_q0), .A1(main_3_q1), .A2(main_3_q2), .A3(main_3_q3), .B0(main_1_q0), .B1(main_1_q1),
    .B2(main_1_q2), .B3(main_1_q3), .out_9(main_2_out_9));
  LED led_1 (.in(main_2_out_9));
  Clock CLK (.out(CLK_out));
  word_main main_3 (
    .CLK(CLK_out), .data_in(WRITE_PASS), .RST(CLEAR_PASS), .HLD(SET_PASS), .Q0(main_3_q0), .Q1(main_3_q1),
    .Q2(main_3_q2), .Q3(main_3_q3));

  // Notes on the sheet:
  //   as 19:39, dia 16/11/24
  //   código feito por João Paulo Ferrari Sant'Ana
  //   a gente vai precisar configurar um outro
  //   porque a gente quer ter uma "senha fixa"
  //   para comparar com a senha do "usuário"
  //   DEFAULT PASS
  //   USER PASS
  //   a gente vai querer pegar toda saida do "USER PASS" usar com alguma porta lógica
  //   repetir o processo com "DEFAULT PASS"
  //   e então pegar a saida dos dois e jogar tudo numa AND
endmodule
