// Logisim project word.circ as structural Verilog: 1 circuit, main circuit main
module main (
  input  CLK,
  input  data_in,
  input  RST,
  input  HLD,
  output Q0,
  output Q1,
  output Q2,
  output Q3
);

  D_Flip_Flop FF0 (.clk(CLK), .D(data_in), .Q(Q0), .en(HLD), .reset(RST));  // open: Qn, preset
  D_Flip_Flop FF1 (.clk(CLK), .D(Q0), .Q(Q1), .en(HLD), .reset(RST));  // open: Qn, preset
  D_Flip_Flop FF2 (.clk(CLK), .D(Q1), .Q(Q2), .en(HLD), .reset(RST));  // open: Qn, preset
  D_Flip_Flop FF3 (.clk(CLK), .D(Q2), .Q(Q3), .en(HLD), .reset(RST));  // open: Qn, preset

  // Notes on the sheet:
  //   porque eu preciso "segurar" (hold) a senha que for configurada
  //   foi escolhido entrada serial e saida paralela porque uma senha funciona desse jeito: 
  //   quando terminamos de digitar o primeiro digito, partimos para o segundo, depois o terceiro e quarto digitos
  //   eu não preciso que o "usuário" tenha acesso aos outros digitos antes da hora
endmodule
