// Logisim project ncheck.circ as structural Verilog: 1 circuit, main circuit main
module main (
  input  B0,
  input  B1,
  input  B2,
  input  B3,
  input  B4,
  input  B5,
  input  B6,
  input  B7,
  output P
);

  wire xor_1_out, xor_2_out, xor_3_out, xor_5_out;

  xor xor_1 (xor_1_out, B0, B1);
  xor xor_2 (xor_2_out, B2, B3);
  xor xor_3 (xor_3_out, B4, B5);
  ExactlyOne xor_4 (.out(P), .in0(xor_1_out), .in1(xor_2_out), .in2(xor_3_out), .in3(xor_5_out));
  xor xor_5 (xor_5_out, B6, B7);

  // Notes on the sheet:
  //   este programa aceita 8 bits que representam números
  //   sua saida é um bit que representa se ele é impar (0) ou par (1)
endmodule
