// Logisim project parity.circ as structural Verilog: 1 circuit, main circuit main
module main (
  input  D0,
  input  D1,
  input  D2,
  input  D3,
  input  D4,
  input  D5,
  input  D6,
  input  D7,
  input  SHIFT_LOAD,
  input  CLK,
  output Q0,
  output Q1,
  output Q2,
  output Q3,
  output Q4,
  output Q5,
  output Q6,
  output Q6_2
);

  wire FF0_q, FF1_q, FF2_q, FF3_q, FF4_q, FF5_q, FF6_q, g2_out, g3_out, g4_out, g5_out, g6_out, g7_out,
       g8_out, g9_out, g10_out, g11_out, g12_2_out, g12_out, g13_2_out, g13_out, not_1_out;

  not not_1 (not_1_out, SHIFT_LOAD);
  and g1 (Q0, D0, not_1_out);
  D_Flip_Flop FF0 (.clk(CLK), .D(Q0), .Q(FF0_q));  // open: Qn, preset, en, reset
  and g5 (g5_out, FF0_q, SHIFT_LOAD);
  and g2 (g2_out, not_1_out, D1);
  or or_1 (Q1, g5_out, g2_out);
  D_Flip_Flop FF1 (.clk(CLK), .D(Q1), .Q(FF1_q));  // open: Qn, preset, en, reset
  and g3 (g3_out, not_1_out, D2);
  and g6 (g6_out, FF1_q, SHIFT_LOAD);
  or or_2 (Q2, g6_out, g3_out);
  D_Flip_Flop FF2 (.clk(CLK), .D(Q2), .Q(FF2_q));  // open: Qn, preset, en, reset
  and g7 (g7_out, FF2_q, SHIFT_LOAD);
  and g4 (g4_out, not_1_out, D3);
  or or_3 (Q3, g7_out, g4_out);
  D_Flip_Flop FF3 (.clk(CLK), .D(Q3), .Q(FF3_q));  // open: Qn, preset, en, reset
  and g9 (g9_out, FF3_q, SHIFT_LOAD);
  and g8 (g8_out, not_1_out, D4);
  or or_4 (Q4, g9_out, g8_out);
  and g11 (g11_out, FF4_q, SHIFT_LOAD);
  D_Flip_Flop FF4 (.clk(CLK), .D(Q4), .Q(FF4_q));  // open: Qn, preset, en, reset
  and g10 (g10_out, not_1_out, D5);
  or or_5 (Q5, g11_out, g10_out);
  D_Flip_Flop FF5 (.clk(CLK), .D(Q5), .Q(FF5_q));  // open: Qn, preset, en, reset
  and g13 (g13_out, FF5_q, SHIFT_LOAD);
  and g12 (g12_out, not_1_out, D6);
  or or_6 (Q6, g13_out, g12_out);
  and g13_2 (g13_2_out, FF6_q, SHIFT_LOAD);
  D_Flip_Flop FF6 (.clk(CLK), .D(Q6), .Q(FF6_q));  // open: Qn, preset, en, reset
  and g12_2 (g12_2_out, not_1_out, D7);
  or or_7 (Q6_2, g13_2_out, g12_2_out);
  D_Flip_Flop FF6_2 (.clk(CLK), .D(Q6_2));  // open: Q, Qn, preset, en, reset

  // Notes on the sheet:
  //   este arquivo foi basado em um slide disponibilizado pelo professor Cesar Giacomini Pentado
  //   este programa aceita 8 bits de forma serial, com sua saida em forma paralela
  //   load é quando queremos carregar um bit dentro deste sistema
  //   shift é quando queremos "multiplicar" o bit para a esquerda
endmodule
