// Logisim project pchecker.circ as structural Verilog: 1 circuit, main circuit main
module main (
  input  B0,
  input  B1,
  input  B2,
  input  B3,
  input  B4,
  input  B5,
  input  B6,
  input  B7,
  input  SHIFT_LOAD,
  output P
);

  wire CLK_out, main_1_p4, main_1_p6, main_1_p8, main_1_p10, main_1_p12, main_1_p14, main_1_p16, not_1_out,
       undriven;

  Clock CLK (.out(CLK_out));
  // parity_main main_1: pin names not known; wires that end beside it: SHIFT_LOAD, CLK_out, B0, main_1_p4, B1, main_1_p6, B2, main_1_p8, B3, main_1_p10, B4, main_1_p12, B5, main_1_p14, B6, main_1_p16
  ncheck_main main_2 (
    .B0(main_1_p4), .B1(main_1_p6), .B2(main_1_p8), .B3(main_1_p10), .B4(main_1_p12), .B5(main_1_p14),
    .B6(main_1_p16), .B7(undriven), .P(P));
  not not_1 (not_1_out, P);
  LED led_1 (.in(not_1_out));

  // Notes on the sheet:
  //   se ligar o número é par, senão é impar
  //   a gente nega aqui porque senão vai dizer que "1, 3, 5 ..." é par
  //   código realizado por João Paulo Ferrari Sant'Ana dia 11/11/24 as 22:17
  //   versão inicial de "parity" realizado pelo professor CESAR GIACOMINI PENTEADO
endmodule
