// Logisim project regress.circ as structural Verilog: 1 circuit, main circuit main
module main (
  input  RST,
  input  PST
);

  wire and_1_out, CLK_out, decodiicador7seg_1_a_2, decodiicador7seg_1_b_2, decodiicador7seg_1_c_2,
       decodiicador7seg_1_d_2, decodiicador7seg_1_e, decodiicador7seg_1_f, decodiicador7seg_1_g, main_1_q0,
       main_1_q1, main_1_q2, main_1_q3, not_1_out, not_2_out, not_3_out, not_4_out;

  Clock CLK (.out(CLK_out));
  contadordesc_main main_1 (
    .CLK(CLK_out), .RST(RST), .PST(PST), .Q0(main_1_q0), .Q1(main_1_q1), .Q2(main_1_q2), .Q3(main_1_q3));
  not not_1 (not_1_out, main_1_q0);
  not not_2 (not_2_out, main_1_q2);
  not not_3 (not_3_out, main_1_q3);
  not not_4 (not_4_out, main_1_q1);
  and and_1 (and_1_out, not_1_out, not_4_out, not_2_out, not_3_out);
  LED led_1 (.in(and_1_out));
  DECODIICADOR7SEG decodiicador7seg_1 (
    .A(main_1_q3), .B(main_1_q2), .C(main_1_q1), .D(main_1_q0), .a_2(decodiicador7seg_1_a_2),
    .b_2(decodiicador7seg_1_b_2), .c_2(decodiicador7seg_1_c_2), .d_2(decodiicador7seg_1_d_2),
    .e(decodiicador7seg_1_e), .f(decodiicador7seg_1_f), .g(decodiicador7seg_1_g));
  _7_Segment_Display u_7_segment_display_1 (
    .g(decodiicador7seg_1_g), .f(decodiicador7seg_1_f), .a(decodiicador7seg_1_a_2),
    .b(decodiicador7seg_1_b_2), .e(decodiicador7seg_1_e), .d(decodiicador7seg_1_d_2),
    .c(decodiicador7seg_1_c_2));  // open: dp

  // Notes on the sheet:
  //   tá dando problema porque eu fiz 4 bit, ou seja, temos 15 números, sendo que esse relogio suporta só 9
endmodule
