// Logisim project contagemregress.circ as structural Verilog: 1 circuit, main circuit main
module main (
  input  CLK,
  input  RST,
  input  PST,
  output Q0,
  output Q1,
  output Q2
);

  wire and_1_out, and_2_out, j_k_ff_1_qn, j_k_ff_2_qn, or_1_out;

  and and_1 (and_1_out, RST, or_1_out);
  J_K_Flip_Flop j_k_ff_1 (
    .J(1'b1), .clk(CLK), .K(1'b1), .Q(Q0), .Qn(j_k_ff_1_qn), .preset(PST), .reset(and_1_out));  // open: en
  or or_1 (or_1_out, Q0, and_1_out);
  J_K_Flip_Flop j_k_ff_2 (
    .J(j_k_ff_1_qn), .clk(CLK), .K(j_k_ff_1_qn), .Q(Q1), .Qn(j_k_ff_2_qn), .preset(PST), .reset(and_1_out));  // open: en
  and and_2 (and_2_out, j_k_ff_1_qn, j_k_ff_2_qn);
  J_K_Flip_Flop j_k_ff_3 (
    .J(and_2_out), .clk(CLK), .K(and_2_out), .Q(Q2), .preset(PST), .reset(and_1_out));  // open: Qn, en

  // Notes on the sheet:
  //   resete tudo
  //   ela "fecha" o flipflop
  //    no começo ou a contagem já estiver no fim
  //   se eu precisar recomeçar tudo no último valor possível,
  //    posso usar a instrução "preset"
  //   se precisar resetar, e a contagem tiver pelo menos um único bit
  //   https://www.electronics-tutorials.ws/counter/count_4.html
  //   o senhor, professor, não especificou a
  //    quantidade de bits, graças a isso: irei usar a  minha vantagem
  //   irei utilizar 3 bits
endmodule
