// Logisim project decrecentcounter.circ as structural Verilog: 1 circuit, main circuit main
module main (
  input  CLK,
  input  RST,
  input  PST,
  output Q0,
  output Q1,
  output Q2,
  output Q3
);

  wire and_1_out, and_2_out, and_3_out, j_k_ff_1_qn, j_k_ff_2_qn, j_k_ff_3_qn, j_k_ff_4_qn, not_1_out,
       not_2_out, not_3_out, not_4_out, or_1_out;

  J_K_Flip_Flop j_k_ff_1 (
    .J(1'b1), .clk(CLK), .K(1'b1), .Q(Q0), .Qn(j_k_ff_1_qn), .preset(or_1_out), .reset(RST));  // open: en
  J_K_Flip_Flop j_k_ff_2 (
    .J(j_k_ff_1_qn), .clk(CLK), .K(j_k_ff_1_qn), .Q(Q1), .Qn(j_k_ff_2_qn), .reset(RST));  // open: preset, en
  and and_1 (and_1_out, j_k_ff_1_qn, j_k_ff_2_qn);
  or or_1 (or_1_out, PST, and_3_out);
  and and_2 (and_2_out, and_1_out, j_k_ff_3_qn);
  J_K_Flip_Flop j_k_ff_3 (
    .J(and_1_out), .clk(CLK), .K(and_1_out), .Q(Q2), .Qn(j_k_ff_3_qn), .reset(RST));  // open: preset, en
  J_K_Flip_Flop j_k_ff_4 (
    .J(and_2_out), .clk(CLK), .K(and_2_out), .Q(Q3), .Qn(j_k_ff_4_qn), .preset(or_1_out), .reset(RST));  // open: en
  and and_3 (and_3_out, not_1_out, not_2_out, not_3_out, not_4_out);
  not not_1 (not_1_out, Q0);
  not not_2 (not_2_out, Q1);
  not not_3 (not_3_out, Q2);
  not not_4 (not_4_out, Q3);

  // Notes on the sheet:
  //   recomeçe manualmente ou quando for zero contagem
  //   versão inicial baseada em: https://www.electronics-tutorials.ws/counter/count_4.html
  //   se for zero, mande um sinal
  //   dica obtida pelo Cesar Giacomini Penteado
endmodule
