// Logisim project regress.circ as structural Verilog: 1 circuit, main circuit main
module main (
  input  RST,
  input  in_2,
  input  in_3,
  input  in_4,
  input  in_5,
  input  in_6,
  input  in_7,
  input  in_8,
  input  in_9,
  input  in_10,
  input  in_11,
  input  in_12,
  input  in_13,
  input  in_14,
  input  in_15,
  input  in_16,
  input  in_17
);

  wire and_1_out, and_2_out, and_3_out, and_4_out, and_5_out, CLK_out, decodiicador7seg_1_a_2,
       decodiicador7seg_1_b_2, decodiicador7seg_1_c_2, decodiicador7seg_1_d_2, decodiicador7seg_1_e,
       decodiicador7seg_1_f, decodiicador7seg_1_g, decodiicador7seg_2_a_2, decodiicador7seg_2_b_2,
       decodiicador7seg_2_c_2, decodiicador7seg_2_d_2, decodiicador7seg_2_e, decodiicador7seg_2_f,
       decodiicador7seg_2_g, decodiicador7seg_3_a_2, decodiicador7seg_3_b_2, decodiicador7seg_3_c_2,
       decodiicador7seg_3_d_2, decodiicador7seg_3_e, decodiicador7seg_3_f, decodiicador7seg_3_g,
       decodiicador7seg_4_a_2, decodiicador7seg_4_b_2, decodiicador7seg_4_c_2, decodiicador7seg_4_d_2,
       decodiicador7seg_4_e, decodiicador7seg_4_f, decodiicador7seg_4_g, main_1_q0, main_1_q1, main_1_q2,
       main_1_q3, main_2_q0, main_2_q1, main_2_q2, main_2_q3, main_3_q0, main_3_q1, main_3_q2, main_3_q3,
       main_4_q0, main_4_q1, main_4_q2, main_4_q3, not_1_out, not_2_out, not_3_out, not_4_out, not_5_out,
       not_6_out, not_7_out, not_8_out, not_9_out, not_10_out, not_11_out, not_12_out, not_13_out,
       not_14_out, not_15_out, not_16_out, or_1_out, or_2_out, or_3_out, or_4_out;

  Clock CLK (.out(CLK_out));
  or or_1 (or_1_out, CLK_out, and_1_out);
  or or_2 (or_2_out, CLK_out, and_2_out);
  or or_3 (or_3_out, CLK_out, and_3_out);
  decrecentcounter_main main_1 (
    .CLK(or_1_out), .RST(RST), .S0(in_2), .Q0(main_1_q0), .S1(in_3), .Q1(main_1_q1), .S3(in_4),
    .Q2(main_1_q2), .S4(in_5), .Q3(main_1_q3));
  or or_4 (or_4_out, CLK_out, and_4_out);
  not not_1 (not_1_out, main_1_q0);
  decrecentcounter_main main_2 (
    .CLK(or_2_out), .RST(RST), .S0(in_6), .Q0(main_2_q0), .S1(in_7), .Q1(main_2_q1), .S3(in_8),
    .Q2(main_2_q2), .S4(in_9), .Q3(main_2_q3));
  decrecentcounter_main main_3 (
    .CLK(or_4_out), .RST(RST), .S0(in_14), .Q0(main_3_q0), .S1(in_15), .Q1(main_3_q1), .S3(in_16),
    .Q2(main_3_q2), .S4(in_17), .Q3(main_3_q3));
  not not_2 (not_2_out, main_1_q1);
  not not_3 (not_3_out, main_1_q2);
  not not_4 (not_4_out, main_1_q3);
  and and_1 (and_1_out, not_1_out, not_2_out, not_3_out, not_4_out);
  not not_5 (not_5_out, main_2_q1);
  not not_6 (not_6_out, main_2_q2);
  not not_7 (not_7_out, main_2_q0);
  and and_2 (and_2_out, not_7_out, not_5_out, not_6_out, not_9_out);
  decrecentcounter_main main_4 (
    .CLK(or_3_out), .RST(RST), .S0(in_10), .Q0(main_4_q0), .S1(in_11), .Q1(main_4_q1), .S3(in_12),
    .Q2(main_4_q2), .S4(in_13), .Q3(main_4_q3));
  not not_8 (not_8_out, main_3_q0);
  DECODIICADOR7SEG decodiicador7seg_1 (
    .A(main_1_q3), .B(main_1_q2), .C(main_1_q1), .D(main_1_q0), .a_2(decodiicador7seg_1_a_2),
    .b_2(decodiicador7seg_1_b_2), .c_2(decodiicador7seg_1_c_2), .d_2(decodiicador7seg_1_d_2),
    .e(decodiicador7seg_1_e), .f(decodiicador7seg_1_f), .g(decodiicador7seg_1_g));
  not not_9 (not_9_out, main_2_q3);
  not not_10 (not_10_out, main_4_q0);
  not not_11 (not_11_out, main_4_q1);
  not not_12 (not_12_out, main_4_q2);
  not not_13 (not_13_out, main_4_q3);
  and and_3 (and_3_out, not_10_out, not_11_out, not_12_out, not_13_out);
  not not_14 (not_14_out, main_3_q1);
  not not_15 (not_15_out, main_3_q3);
  not not_16 (not_16_out, main_3_q2);
  and and_4 (and_4_out, not_8_out, not_14_out, not_16_out, not_15_out);
  _7_Segment_Display u_7_segment_display_1 (
    .g(decodiicador7seg_1_g), .f(decodiicador7seg_1_f), .a(decodiicador7seg_1_a_2),
    .b(decodiicador7seg_1_b_2), .e(decodiicador7seg_1_e), .d(decodiicador7seg_1_d_2),
    .c(decodiicador7seg_1_c_2));  // open: dp
  DECODIICADOR7SEG decodiicador7seg_2 (
    .A(main_2_q3), .B(main_2_q2), .C(main_2_q1), .D(main_2_q0), .a_2(decodiicador7seg_2_a_2),
    .b_2(decodiicador7seg_2_b_2), .c_2(decodiicador7seg_2_c_2), .d_2(decodiicador7seg_2_d_2),
    .e(decodiicador7seg_2_e), .f(decodiicador7seg_2_f), .g(decodiicador7seg_2_g));
  DECODIICADOR7SEG decodiicador7seg_3 (
    .A(main_3_q3), .B(main_3_q2), .C(main_3_q1), .D(main_3_q0), .a_2(decodiicador7seg_3_a_2),
    .b_2(decodiicador7seg_3_b_2), .c_2(decodiicador7seg_3_c_2), .d_2(decodiicador7seg_3_d_2),
    .e(decodiicador7seg_3_e), .f(decodiicador7seg_3_f), .g(decodiicador7seg_3_g));
  _7_Segment_Display u_7_segment_display_2 (
    .g(decodiicador7seg_2_g), .f(decodiicador7seg_2_f), .a(decodiicador7seg_2_a_2),
    .b(decodiicador7seg_2_b_2), .e(decodiicador7seg_2_e), .d(decodiicador7seg_2_d_2),
    .c(decodiicador7seg_2_c_2));  // open: dp
  DECODIICADOR7SEG decodiicador7seg_4 (
    .A(main_4_q3), .B(main_4_q2), .C(main_4_q1), .D(main_4_q0), .a_2(decodiicador7seg_4_a_2),
    .b_2(decodiicador7seg_4_b_2), .c_2(decodiicador7seg_4_c_2), .d_2(decodiicador7seg_4_d_2),
    .e(decodiicador7seg_4_e), .f(decodiicador7seg_4_f), .g(decodiicador7seg_4_g));
  _7_Segment_Display u_7_segment_display_3 (
    .g(decodiicador7seg_3_g), .f(decodiicador7seg_3_f), .a(decodiicador7seg_3_a_2),
    .b(decodiicador7seg_3_b_2), .e(decodiicador7seg_3_e), .d(decodiicador7seg_3_d_2),
    .c(decodiicador7seg_3_c_2));  // open: dp
  _7_Segment_Display u_7_segment_display_4 (
    .g(decodiicador7seg_4_g), .f(decodiicador7seg_4_f), .a(decodiicador7seg_4_a_2),
    .b(decodiicador7seg_4_b_2), .e(decodiicador7seg_4_e), .d(decodiicador7seg_4_d_2),
    .c(decodiicador7seg_4_c_2));  // open: dp
  and and_5 (and_5_out, and_1_out, and_2_out, and_3_out, and_4_out);
  LED led_1 (.in(and_5_out));

  // Notes on the sheet:
  //   Sinal de fim da contagem
  //   Sinal de fim da contagem
  //   Sinal de fim da contagem
  //   Sinal de fim da contagem
  //   dica de como desenvolver circuto obtido a partir do professor CESAR GIACOMINI PENTEADO
  //   código realizado por João Paulo  Ferrari Sant'Ana, dia 15/11/24 ás 17:02
  //   código atualizado por João Paulo Ferrari Sant' Ana, dia 20/11/24 as 9:20 da manhã
  //   dia 11/11/24 as 10:20PM
  //   fim da contagem
endmodule
