// Logisim project serial-entry-paralel-exit.circ as structural Verilog: 1 circuit, main circuit main
module main (
  input  CLK,
  input  data_in,
  input  RST,
  output Q0,
  output Q1,
  output Q2,
  output Q3
);

  D_Flip_Flop FF0 (.clk(CLK), .D(data_in), .Q(Q0), .reset(RST));  // open: Qn, preset, en
  D_Flip_Flop FF1 (.clk(CLK), .D(Q0), .Q(Q1), .reset(RST));  // open: Qn, preset, en
  D_Flip_Flop FF2 (.clk(CLK), .D(Q1), .Q(Q2), .reset(RST));  // open: Qn, preset, en
  D_Flip_Flop FF3 (.clk(CLK), .D(Q2), .Q(Q3), .reset(RST));  // open: Qn, preset, en

  // Notes on the sheet:
  //   mas por hora, isso já serve
  //   adento: seria melhor se eu colocasse um RST para cada flip flop
endmodule
