// Logisim project subtr2.circ as structural Verilog: 1 circuit, main circuit main
module main (
  input  c,
  input  b,
  input  a,
  input  in_4,
  input  in_5,
  input  in_6,
  input  in_7,
  input  in_8,
  input  in_9,
  output out_10,
  output OK,
  output out_12,
  output out_13,
  output out_14,
  output OK_2,
  output out_16,
  output out_17,
  output out_18,
  output OK_3,
  output out_20,
  output out_21,
  output out_22,
  output OK_4,
  output out_24,
  output out_25
);

  wire and_5_out, and_6_out, and_7_out, and_8_out, not_1_out, not_2_out, not_3_out, not_4_out, not_5_out,
       not_6_out, not_7_out, not_8_out;

  xor xor_1 (out_10, b, a);
  not not_1 (not_1_out, b);
  xor xor_2 (out_14, in_4, in_5);
  not not_2 (not_2_out, in_4);
  xor xor_3 (out_18, in_6, in_7);
  not not_3 (not_3_out, in_6);
  xor xor_4 (out_22, in_8, in_9);
  not not_4 (not_4_out, in_8);
  LED led_1 (.in(out_10));
  and and_1 (out_12, not_1_out, a);
  LED led_2 (.in(out_14));
  and and_2 (out_16, not_2_out, in_5);
  LED led_3 (.in(out_18));
  and and_3 (out_20, not_3_out, in_7);
  LED led_4 (.in(out_22));
  and and_4 (out_24, not_4_out, in_9);
  LED led_5 (.in(out_12));
  LED led_6 (.in(out_16));
  LED led_7 (.in(out_20));
  LED led_8 (.in(out_24));
  not not_5 (not_5_out, out_10);
  not not_6 (not_6_out, out_14);
  not not_7 (not_7_out, out_18);
  not not_8 (not_8_out, out_22);
  xor xor_5 (OK, c, out_10);
  and and_5 (and_5_out, not_5_out, c);
  xor xor_6 (OK_2, out_13, out_14);
  xor xor_7 (OK_3, out_17, out_18);
  LED led_9 (.in(OK_4));
  xor xor_8 (OK_4, out_21, out_22);
  and and_6 (and_6_out, not_8_out, out_21);
  LED led_10 (.in(OK));
  LED led_11 (.in(OK_2));
  and and_7 (and_7_out, not_6_out, out_13);
  LED led_12 (.in(OK_3));
  and and_8 (and_8_out, not_7_out, out_17);
  or or_1 (out_13, and_5_out, out_12);
  or or_2 (out_17, and_7_out, out_16);
  or or_3 (out_21, and_8_out, out_20);
  or or_4 (out_25, and_6_out, out_24);
endmodule
